// Digital circuit Ctrl_ULA.dig as structural Verilog
module Ctrl_ULA (
  input  [1:0] Cont2ULA,
  input  [2:0] Func,
  output Ain,
  output Bin,
  output Cin,
  output [1:0] ControleULA
);

  wire and_1_out, and_5_out, and_7_out, not_1_out, not_2_out, not_3_out, not_4_out, not_5_out, undriven,
       undriven_2, undriven_3;

  not not_1 (not_1_out, Func[1]);
  not not_2 (not_2_out, Func[2]);
  not not_3 (not_3_out, Cont2ULA[1]);
  not not_4 (not_4_out, Func[0]);
  not not_5 (not_5_out, Cont2ULA[0]);
  and and_1 (and_1_out, not_5_out, not_4_out, Func[1], Func[2]);
  or or_1 (ControleULA[0], Cont2ULA[0], Cont2ULA[1], not_1_out);
  // And and_2 has open pins: In_1=not_5_out, In_2=not_3_out, In_3=not_4_out, In_4=Func[1], In_5=Func[2], out=open
  // And and_3 has open pins: In_1=not_5_out, In_2=not_3_out, In_3=Func[0], In_4=not_2_out, out=open
  // And and_4 has open pins: In_1=not_5_out, In_2=not_3_out, In_3=Func[0], In_4=not_4_out, out=open
  and and_5 (and_5_out, not_5_out, Func[2]);
  and and_6 (Ain, not_5_out, not_3_out, Func[0], Func[1]);
  and and_7 (and_7_out, Func[0], Func[1], not_5_out);
  or or_2 (Cin, and_5_out, Cont2ULA[1]);
  or or_3 (Bin, and_1_out, Cont2ULA[1], and_7_out);
  or or_4 (ControleULA[1], undriven, undriven_2, undriven_3);
  // Pins of 1 and 2 bits meet at ControleULA

  // Notes on the sheet:
  //   Ain = ~C0*~C1*F0*F1
  //   Bin = ~F0*~F1*F2*~C0 + F0*F1*~C0 + C1
  //   Cin = C1 + ~C0*F2
  //   Op_0 = C1+C0+~F1
  //   Op_1 = ~C0*~C1*~F0*F1*F2 + ~C0*~C1*F0*~F2 + ~C0*~C1*F0*~F1
  //   F2, F1, F0, C1, C0
  //   Negado, Normal
endmodule
