// Digital circuit Processador acho.dig as structural Verilog
module Processador_acho (
  input  in_1,
  input  in_2,
  input  in_3,
  input  [1:0] in_4,
  input  [1:0] in_5,
  input  [1:0] in_6,
  input  [1:0] in_7,
  input  [1:0] in_8,
  input  in_9,
  input  in_10,
  input  in_11,
  input  in_12,
  input  in_13,
  input  in_14,
  input  in_15,
  input  in_16,
  input  in_17
);

  wire button_1_out, ctrl_ula_1_ain, ctrl_ula_1_bin, ctrl_ula_1_cin;
  wire [1:0] ctrl_ula_1_controleula;
  wire [2:0] multiplexer_3_out;
  wire [3:0] Oper;
  wire [11:0] IR_q;
  wire [15:0] Ext_Sinal_out, IP_q, MEM_WRT, \Memória_d , multiplexer_1_out, multiplexer_2_out,
       multiplexer_4_out, multiplexer_5_out, Reg_Dados_Mem_q, reginaldos_1_saireginaldo1,
       reginaldos_1_saireginaldo2, \rol_1_saída_rol , To_PC, \ula_1_saída_geral , ULA_A_q, ULA_out;

  Button button_1 (.out(button_1_out));
  Register #(.Bits(16)) IP (.D(To_PC), .C(button_1_out), .en(in_10), .Q(IP_q));
  Multiplexer #(.Bits(16)) multiplexer_1 (.sel(in_1), .in_0(IP_q), .in_1(ULA_out), .out(multiplexer_1_out));
  RAMDualPort #(.AddrBits(16), .Bits(16)) \Memória  (
    .A(multiplexer_1_out), .Din(MEM_WRT), .str(in_16), .C(button_1_out), .ld(in_17), .D(\Memória_d ));
  Register #(.Bits(16)) Reg_Dados_Mem (.D(\Memória_d ), .C(button_1_out), .en(in_9), .Q(Reg_Dados_Mem_q));
  Register #(.Bits(16)) IR (.D(\Memória_d ), .C(button_1_out), .en(in_11), .Q({Oper, IR_q}));
  Multiplexer #(.Bits(16)) multiplexer_2 (.sel(in_2), .in_0(ULA_out), .in_1(Reg_Dados_Mem_q), .out(multiplexer_2_out));
  Multiplexer #(.Selector_Bits(2), .Bits(3)) multiplexer_3 (
    .sel(in_6), .in_0(IR_q[11:9]), .in_1(IR_q[8:6]), .in_2(IR_q[5:3]), .in_3(IR_q[5:3]),
    .out(multiplexer_3_out));
  Reginaldos reginaldos_1 (
    .Leitura1(IR_q[11:9]), .Leitura2(IR_q[8:6]), .Escrita(multiplexer_3_out),
    .DadosReginaldo(multiplexer_2_out), .Clock(button_1_out), .EscrevReginaldo(in_15),
    .SaiReginaldo1(reginaldos_1_saireginaldo1), .SaiReginaldo2(reginaldos_1_saireginaldo2));
  BitExtender Ext_Sinal (.in({Oper, IR_q[11:8]}), .out(Ext_Sinal_out));
  Register #(.Bits(16)) ULA_B (.D(reginaldos_1_saireginaldo2), .C(button_1_out), .en(in_12), .Q(MEM_WRT));
  Register #(.Bits(16)) ULA_A (.D(reginaldos_1_saireginaldo1), .C(button_1_out), .en(in_13), .Q(ULA_A_q));
  Ctrl_ULA ctrl_ula_1 (
    .Op_ULA(in_4), .Func(IR_q[2:0]), .Ain(ctrl_ula_1_ain), .Bin(ctrl_ula_1_bin), .Cin(ctrl_ula_1_cin),
    .ControleULA(ctrl_ula_1_controleula));
  Multiplexer #(.Selector_Bits(2), .Bits(16)) multiplexer_4 (
    .sel(in_8), .in_0(16'h1), .in_1(MEM_WRT), .in_2(16'h1), .in_3(Ext_Sinal_out), .out(multiplexer_4_out));
  Multiplexer #(.Bits(16)) multiplexer_5 (.sel(in_3), .in_0(IP_q), .in_1(ULA_A_q), .out(multiplexer_5_out));
  ULA ula_1 (
    .A(multiplexer_5_out), .B(multiplexer_4_out), .Ainv(ctrl_ula_1_ain), .Binv(ctrl_ula_1_bin),
    .Cin(ctrl_ula_1_cin), .OP(ctrl_ula_1_controleula), .\Saída_geral (\ula_1_saída_geral ));  // open: Cout, Zero, Overflow
  Register #(.Bits(16)) u_ULA_out (.D(\ula_1_saída_geral ), .C(button_1_out), .en(in_14), .Q(ULA_out));
  Rol rol_1 (.Controle_Rol(in_5), .Entrada_Rol(multiplexer_5_out), .\Saída_Rol (\rol_1_saída_rol ));
  Multiplexer #(.Selector_Bits(2), .Bits(16)) multiplexer_6 (
    .sel(in_7), .in_0(ULA_out), .in_1(\rol_1_saída_rol ), .in_2(16'h1), .in_3(16'h1), .out(To_PC));

  // Other names for the same wires on the sheet: Escreve_REG = in_15; IP_REG_EN = in_10; IR_REG_EN = in_11;
  //   MEM_ld = in_17; MEM_PARA_REG = in_2; MEM_str = in_16; MUX_PC = in_1; Mux_RegA = in_3; MUX_ULA[1:0] = in_7;
  //   Op_ULA[1:0] = in_4; Reg_Dados_Mem_EN = in_9; REG_ULA_A_EN = in_13; REG_ULA_B_EN = in_12; REG_ULA_OUT_EN = in_14;
  //   Rol_ctrl[1:0] = in_5; ULA_B_SELECT[1:0] = in_8; WRT_Select[1:0] = in_6

  // Notes on the sheet:
  //   1 Bit - MUX
  //   2 Bits - CTRL
  //   2 Bits - MUX
  //   Registradores - Enable
  //   1 Bit - CTRL
endmodule
