// Digital circuit Reginaldos.dig as structural Verilog
module Reginaldos (
  input  [2:0] Leitura1,
  input  [2:0] Leitura2,
  input  [2:0] Escrita,
  input  [15:0] DadosReginaldo,
  input  Clock,
  input  EscrevReginaldo,
  output [15:0] SaiReginaldo1,
  output [15:0] SaiReginaldo2
);

  wire habilida_escrita_1__2, habilida_escrita_1__3, habilida_escrita_1__4, habilida_escrita_1__5,
       habilida_escrita_1__6, habilida_escrita_1__7;
  wire [15:0] A_q, B_q, C_q, D_q, E_q, Flags_q;

  habilida_Escrita habilida_escrita_1 (
    .EscrevReginaldo(EscrevReginaldo), .Escrita(Escrita), ._2(habilida_escrita_1__2),
    ._3(habilida_escrita_1__3), ._4(habilida_escrita_1__4), ._5(habilida_escrita_1__5),
    ._6(habilida_escrita_1__6), ._7(habilida_escrita_1__7));
  Register #(.Bits(16)) A (.D(DadosReginaldo), .C(Clock), .en(habilida_escrita_1__2), .Q(A_q));
  Register #(.Bits(16)) B (.D(DadosReginaldo), .C(Clock), .en(habilida_escrita_1__3), .Q(B_q));
  Register #(.Bits(16)) C (.D(DadosReginaldo), .C(Clock), .en(habilida_escrita_1__4), .Q(C_q));
  Register #(.Bits(16)) D (.D(DadosReginaldo), .C(Clock), .en(habilida_escrita_1__5), .Q(D_q));
  Register #(.Bits(16)) E (.D(DadosReginaldo), .C(Clock), .en(habilida_escrita_1__6), .Q(E_q));
  Register #(.Bits(16)) Flags (.D(DadosReginaldo), .C(Clock), .en(habilida_escrita_1__7), .Q(Flags_q));
  Multiplexer #(.Selector_Bits(3), .Bits(16)) multiplexer_1 (
    .sel(Leitura1), .in_0({16{1'b0}}), .in_1(16'h1), .in_2(A_q), .in_3(B_q), .in_4(C_q), .in_5(D_q),
    .in_6(E_q), .in_7(Flags_q), .out(SaiReginaldo1));
  Multiplexer #(.Selector_Bits(3), .Bits(16)) multiplexer_2 (
    .sel(Leitura2), .in_0({16{1'b0}}), .in_1(16'h1), .in_2(A_q), .in_3(B_q), .in_4(C_q), .in_5(D_q),
    .in_6(E_q), .in_7(Flags_q), .out(SaiReginaldo2));
endmodule
