// Digital circuit Rol.dig as structural Verilog
module Rol (
  input  [1:0] Controle_Rol,
  input  [15:0] Entrada_Rol,
  output [15:0] \Saída_Rol 
);

  wire [15:0] barrelshifter_1_out, barrelshifter_2_out, barrelshifter_3_out, barrelshifter_4_out;

  BarrelShifter #(.Bits(16), .direction("right")) barrelshifter_1 (
    .in(Entrada_Rol), .shift(5'b00001), .out(barrelshifter_1_out));
  BarrelShifter #(.Bits(16)) barrelshifter_2 (.in(Entrada_Rol), .shift(5'b00001), .out(barrelshifter_2_out));
  BarrelShifter #(.Bits(16), .barrelShifterMode("rotate"), .direction("right")) barrelshifter_3 (
    .in(Entrada_Rol), .shift(5'b00001), .out(barrelshifter_3_out));
  BarrelShifter #(.Bits(16), .barrelShifterMode("rotate")) barrelshifter_4 (
    .in(Entrada_Rol), .shift(5'b00001), .out(barrelshifter_4_out));
  Multiplexer #(.Selector_Bits(2), .Bits(16)) multiplexer_1 (
    .sel(Controle_Rol), .in_0(barrelshifter_1_out), .in_1(barrelshifter_2_out), .in_2(barrelshifter_3_out),
    .in_3(barrelshifter_4_out), .out(\Saída_Rol ));
endmodule
