// Digital circuit UC.dig as structural Verilog
module UC (
  input  [3:0] Oper,
  output [1:0] Op_ULA,
  output Reg_write,
  output MUX_PC,
  output MUX_REGA,
  output MUX_REG2,
  output MUX_ULA,
  output ORIG_PC,
  output Rol_ctrl
);


  assign MUX_PC = Oper[1];
  assign MUX_REG2 = Oper[1];
  assign MUX_REGA = Oper[1];
  assign MUX_ULA = Oper[0];
  assign Op_ULA = Oper[3:2];
  assign ORIG_PC = Oper[0];
  assign Reg_write = Oper[1];
  assign Rol_ctrl = Oper[0];

  // Notes on the sheet:
  //   Oper: 4 primeiros bits da linha de comando
endmodule
