// Digital circuit habilida Escrita.dig as structural Verilog
module habilida_Escrita (
  input  EscrevReginaldo,
  input  [2:0] Escrita,
  output _2,
  output _3,
  output _4,
  output _5,
  output _6,
  output _7
);

  wire decoder_1_out_2, decoder_1_out_3, decoder_1_out_4, decoder_1_out_5, decoder_1_out_6, decoder_1_out_7;

  Decoder #(.Selector_Bits(3)) decoder_1 (
    .sel(Escrita), .out_2(decoder_1_out_2), .out_3(decoder_1_out_3), .out_4(decoder_1_out_4),
    .out_5(decoder_1_out_5), .out_6(decoder_1_out_6), .out_7(decoder_1_out_7));  // open: out_0, out_1
  and and_1 (_2, decoder_1_out_2, EscrevReginaldo);
  and and_2 (_3, decoder_1_out_3, EscrevReginaldo);
  and and_3 (_4, decoder_1_out_4, EscrevReginaldo);
  and and_4 (_5, decoder_1_out_5, EscrevReginaldo);
  and and_5 (_6, decoder_1_out_6, EscrevReginaldo);
  and and_6 (_7, decoder_1_out_7, EscrevReginaldo);
endmodule
